// Logisim project procesor.circ as structural Verilog
module Procesor (
  input  [15:0] in_1,
  input  LD,
  input  [15:0] in_3,
  output [15:0] out_4,
  output [7:0] out_5
);

  wire CLK_out;
  wire [2:0] main_1_a1, main_1_a2;
  wire [3:0] main_1_com;
  wire [7:0] main_1_ma, registers_1_value1, registers_1_value2;

  Clock CLK (.out(CLK_out));
  CU_main main_1 (.Instruction(in_3), .COM(main_1_com), .A1(main_1_a1), .A2(main_1_a2), .MA(main_1_ma));
  RAM #(.dataWidth(16), .bus("separate")) ram_1 (
    .addr(main_1_ma), .din(in_1), .data(out_4), .clk(CLK_out), .ld(LD));  // open: str, sel, clr
  Registers registers_1 (
    .DESTINATION(3'b000), .VALUE1(registers_1_value1), .CLK(CLK_out), .SOURCE1(main_1_a1),
    .VALUE2(registers_1_value2), .SOURCE2(main_1_a2));  // open: in_6, MEM
  ALU alu_1 (
    .R1__Value_of_first_register(registers_1_value1), .R2__Value_of_second_register(registers_1_value2),
    .OUT__ALU_output(out_5), .COM__Value_of_command__0000_to_1111(main_1_com));  // open: FLAGS_ZCOP
endmodule
